# Fritzing sketch SoundCard (saved by Fritzing 0.9.3b)
circuit board: 7.31228cm x 3.53276cm
breadboards: 1

parts:
  Composant1 = Adafruit Stereo 2.8W Class D Audio Amplifier - I2C Control AGC - TPA2016 [part_number="Adafruit #1712"]
  Composant2 = Adafruit UDA1334 I2S DAC [part_number="Adafruit #3678"]
  J3 = JST-03JQ-BT [part_number=JST-JQ-BT package=THT]
  J4 = female pin header, 4 pins [form="♀ (female)"]
  J5 = female pin header, 2 pins [form="♀ (female)"]
  J6 = female pin header, 2 pins [form="♀ (female)"]
  J7 = rounded female pin header, 1 pin [form="♀ (female rounded)"]

nets:
  N1: Composant1.OUT_L_N, J6.pin1
  N2: Composant1.OUT_L_P, J6.pin2
  N3: Composant1.OUT_R_P, J5.pin2
  N4: Composant1.OUT_R_N, J5.pin1
  VDD: Composant1.VDD, Composant2.3.3V
  N5: Composant1.GND, Composant1.IN_R_N, Composant1.IN_L_N, Composant2.AGND
  N6: Composant1.SHUTDOWN, J7.pin1
  N7: Composant1.IN_R_P, Composant2.OUTR
  N8: Composant1.IN_L_P, Composant2.OUTL
  N9: Composant1.SCL, J4.pin2
  N10: Composant1.SDA, J4.pin3
  N11: Composant1.I2C_VCC, Composant2.VIN, J4.pin4
  N12: Composant2.GND, J4.pin1
  N13: Composant2.WORDSEL_IN, J3.pin1
  N14: Composant2.DATA_IN, J3.pin2
  N15: Composant2.BITCLK_IN, J3.pin3

notes:
  BCLK DIN WSEL

custom parts:
  Adafruit Stereo 2.8W Class D Audio Amplifier - I2C Control AGC - TPA2016: A mini class D with AGC and I2C control? Yes please! This incredibly small stereo amplifier is surprisingly powerful. It is able to deliver 2 x 2.8W channels into 4 ohm impedance speakers (@ 10% THD) and it has a i2c control interface as well as an AGC (automatic gain control) system to keep your audio from clipping or distorting. If you don't want to use I2C to control it, it does start up on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
  Adafruit UDA1334 I2S DAC: This fully-featured UDA1334A I2S Stereo DAC breakout is a perfect match for any I2S-output audio interface. It's affordable but sounds great! The NXP UDA1334A is a jack-of-all-I2S-trades: you can use 3.3V - 5V logic levels (a rarity), and can process multiple different formats by setting two pins to high or low. The DAC will process data immediately, and give you a clear, analog, stereo line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
