# Fritzing sketch piClock (saved by Fritzing 0.9.2b)
circuit board: 8.46667cm x 5.64444cm
breadboards: 1

parts:
  T5 = Basic FET N-Channel [package="TO220 [THT]"]
  T6 = Basic FET N-Channel [package="TO220 [THT]"]
  T7 = Basic FET N-Channel [package="TO220 [THT]"]
  T8 = Basic FET N-Channel [package="TO220 [THT]"]
  Rp5 = Resistor [tolerance=±5% resistance=1k package=THT]
  Rp6 = Resistor [tolerance=±5% resistance=1k package=THT]
  Rp7 = Resistor [tolerance=±5% resistance=1k package=THT]
  Rp8 = Resistor [tolerance=±5% resistance=1k package=THT]
  Composant1 = Arduino Nano (Rev3.0)
  J1 = rounded female pin header, 4 pins [form="♀ (female rounded)"]
  J2 = rounded female pin header, 4 pins [form="♀ (female rounded)"]
  R1 = Resistor [tolerance=±1% resistance=270 package=THT]
  R2 = Resistor [tolerance=±1% resistance=270 package=THT]
  R3 = Resistor [tolerance=±1% resistance=150 package=THT]
  R4 = Resistor [tolerance=±1% resistance=150 package=THT]
  Raspberry_Pi1 = Raspberry Pi 2
  C1 = Ceramic Capacitor [capacitance=33nF voltage=16V package="200 mil [THT, multilayer]"]
  C2 = Ceramic Capacitor [capacitance=33nF voltage=16V package="200 mil [THT, multilayer]"]
  C3 = Electrolytic Capacitor [capacitance=10µF voltage=20V package="100 mil [THT, electrolytic]"]
  C4 = Electrolytic Capacitor [capacitance=10µF voltage=20V package="100 mil [THT, electrolytic]"]
  D1 = Rectifier Diode [part_number=1N4007 package="300 mil [THT]"]
  D2 = Rectifier Diode [part_number=1N4007 package="300 mil [THT]"]
  D3 = Rectifier Diode [part_number=1N4007 package="300 mil [THT]"]
  D4 = Rectifier Diode [part_number=1N4007 package="300 mil [THT]"]
  J3 = rounded female pin header, 2 pins [form="♀ (female rounded)"]
  J4 = rounded female pin header, 2 pins [form="♀ (female rounded)"]
  J5 = rounded female pin header, 6 pins [form="♀ (female rounded)"]
  CD1 = CD4051
  J6 = rounded female pin header, 12 pins [form="♀ (female rounded)"]
  J7 = rounded female pin header, 13 pins [form="♀ (female rounded)"]

nets:
  N1: T5.gate, T8.gate, Rp7.Pin_1, Rp8.Pin_1, J1.pin1, Raspberry_Pi1.3v3, D1.cathode, D2.cathode, J5.pin5
  N2: T5.drain, T7.drain
  N3: T5.source, Rp7.Pin_0, J1.pin2, Raspberry_Pi1.GPIO2
  5V: T6.gate, T7.gate, Rp5.Pin_0, Rp6.Pin_0, Composant1.5V, J2.pin1, Raspberry_Pi1.5V, CD1.In/Out, CD1.VDD
  N4: T6.drain, T8.drain
  N5: T6.source, Rp6.Pin_1, Composant1.A5, J2.pin3
  N6: T7.source, Rp5.Pin_1, Composant1.A4, J2.pin2
  N7: T8.source, Rp8.Pin_0, J1.pin3, Raspberry_Pi1.GPIO3
  GND: Composant1.GND, J1.pin4, J2.pin4, R3.Pin_1, R4.Pin_0, Raspberry_Pi1.GND, C1.0, C2.0, D3.anode, D4.anode, J3.pin2, J4.pin2, J5.pin6, CD1.VSS
  N8: Composant1.A3, CD1.Input_C
  N9: Composant1.A2, CD1.Input_B
  N10: Composant1.A1, CD1.Input_A
  N11: Composant1.A0, CD1.Inhibit
  N12: R1.Pin_0, R3.Pin_0, C1.1, C3.+
  N13: R1.Pin_1, Raspberry_Pi1.GPIO19
  N14: R2.Pin_0, R4.Pin_1, C2.1, C4.+
  N15: R2.Pin_1, Raspberry_Pi1.GPIO18
  N16: Raspberry_Pi1.GPIO17, J5.pin4
  N17: Raspberry_Pi1.GPIO27, J5.pin3
  N18: Raspberry_Pi1.GPIO22, J5.pin2
  N19: Raspberry_Pi1.GPIO23, J5.pin1
  N20: C3.-, D2.anode, D3.cathode, J3.pin1
  N21: C4.-, D1.anode, D4.cathode, J4.pin1
  N22: CD1.Chan_4, J7.pin13
  N23: CD1.Chan_6, J7.pin3
  N24: CD1.Chan_7, J7.pin2
  N25: CD1.Chan_5, J7.pin1
  N26: CD1.Chan_3, J6.pin12
  N27: CD1.Chan_0, J6.pin5
  N28: CD1.Chan_1, J6.pin4
  N29: CD1.Chan_2, J6.pin1

notes:
  I2C 3V3
  3V3 SDA SDC GND
  I2C 5V
  5V SDA SDC GND
