# Fritzing sketch piClock2 (saved by Fritzing 0.9.2b)
circuit board: 12.5217cm x 4.80992cm
breadboards: 1

parts:
  T5 = Basic FET N-Channel [package="TO220 [THT]"]
  T6 = Basic FET N-Channel [package="TO220 [THT]"]
  T7 = Basic FET N-Channel [package="TO220 [THT]"]
  T8 = Basic FET N-Channel [package="TO220 [THT]"]
  Rp5 = Resistor [tolerance=±5% resistance=1k package=THT]
  Rp6 = Resistor [tolerance=±5% resistance=1k package=THT]
  Rp7 = Resistor [tolerance=±5% resistance=1k package=THT]
  Rp8 = Resistor [tolerance=±5% resistance=1k package=THT]
  Composant1 = Arduino Nano (Rev3.0)
  J1 = rounded female pin header, 4 pins [form="♀ (female rounded)"]
  J2 = rounded female pin header, 4 pins [form="♀ (female rounded)"]
  R1 = Resistor [tolerance=±1% resistance=270 package=THT]
  R2 = Resistor [tolerance=±1% resistance=270 package=THT]
  R3 = Resistor [tolerance=±1% resistance=150 package=THT]
  R4 = Resistor [tolerance=±1% resistance=150 package=THT]
  Raspberry_Pi1 = Raspberry Pi 2
  C1 = Ceramic Capacitor [capacitance=33nF voltage=16V package="200 mil [THT, multilayer]"]
  C2 = Ceramic Capacitor [capacitance=33nF voltage=16V package="200 mil [THT, multilayer]"]
  C3 = Electrolytic Capacitor [capacitance=10µF voltage=20V package="100 mil [THT, electrolytic]"]
  C4 = Electrolytic Capacitor [capacitance=10µF voltage=20V package="100 mil [THT, electrolytic]"]
  D1 = Rectifier Diode [part_number=1N4007 package="300 mil [THT]"]
  D2 = Rectifier Diode [part_number=1N4007 package="300 mil [THT]"]
  D3 = Rectifier Diode [part_number=1N4007 package="300 mil [THT]"]
  D4 = Rectifier Diode [part_number=1N4007 package="300 mil [THT]"]
  J3 = rounded female pin header, 2 pins [form="♀ (female rounded)"]
  J4 = rounded female pin header, 2 pins [form="♀ (female rounded)"]
  J5 = rounded female pin header, 6 pins [form="♀ (female rounded)"]
  J6 = rounded female pin header, 12 pins [form="♀ (female rounded)"]
  J7 = rounded female pin header, 13 pins [form="♀ (female rounded)"]
  U1 = 74HC4051 [package=so16]

nets:
  N1: T5.gate, T8.gate, Rp7.Pin_1, Rp8.Pin_1, J1.pin1, Raspberry_Pi1.3v3, D1.cathode, D2.cathode, J5.pin5
  N2: T5.drain, T7.drain
  N3: T5.source, Rp7.Pin_0, J1.pin2, Raspberry_Pi1.GPIO2
  5V: T6.gate, T7.gate, Rp5.Pin_0, Rp6.Pin_0, Composant1.5V, J2.pin1, Raspberry_Pi1.5V, U1.IO, U1.VDD
  N4: T6.drain, T8.drain
  N5: T6.source, Rp6.Pin_1, Composant1.A5, J2.pin3
  N6: T7.source, Rp5.Pin_1, Composant1.A4, J2.pin2
  N7: T8.source, Rp8.Pin_0, J1.pin3, Raspberry_Pi1.GPIO3
  GND: Composant1.GND, J1.pin4, J2.pin4, R3.Pin_1, R4.Pin_0, Raspberry_Pi1.GND, C1.0, C2.0, D3.anode, D4.anode, J3.pin2, J4.pin2, J5.pin6, U1.VSS
  N8: Composant1.D2, J6.pin10, J7.pin12
  N9: Composant1.D3, J6.pin7, J7.pin11
  N10: Composant1.D4, J6.pin9, J7.pin10
  N11: Composant1.D5, J6.pin8, J7.pin9
  N12: Composant1.D6, J7.pin8
  N13: Composant1.D7, J6.pin6, J7.pin7
  N14: Composant1.D8, J6.pin2, J7.pin6
  N15: Composant1.D9, J6.pin3, J7.pin5
  N16: Composant1.D10, J6.pin11, J7.pin4
  N17: Composant1.A3, U1.C
  N18: Composant1.A2, U1.B
  N19: Composant1.A1, U1.A
  N20: Composant1.A0, U1.INH
  N21: R1.Pin_0, R3.Pin_0, C1.1, C3.+
  N22: R1.Pin_1, Raspberry_Pi1.GPIO19
  N23: R2.Pin_0, R4.Pin_1, C2.1, C4.+
  N24: R2.Pin_1, Raspberry_Pi1.GPIO18
  N25: Raspberry_Pi1.GPIO17, J5.pin4
  N26: Raspberry_Pi1.GPIO27, J5.pin3
  N27: Raspberry_Pi1.GPIO22, J5.pin2
  N28: Raspberry_Pi1.GPIO23, J5.pin1
  N29: C3.-, D2.anode, D3.cathode, J3.pin1
  N30: C4.-, D1.anode, D4.cathode, J4.pin1
  N31: J6.pin1, U1.IO2
  N32: J6.pin4, U1.IO1
  N33: J6.pin5, U1.IO0
  N34: J6.pin12, U1.IO3
  N35: J7.pin1, U1.IO5
  N36: J7.pin2, U1.IO7
  N37: J7.pin3, U1.IO6
  N38: J7.pin13, U1.IO4

notes:
  I2C 3V3
  3V3 SDA SDC GND
  I2C 5V
  5V SDA SDC GND
