# Fritzing sketch piClock3 (saved by Fritzing 0.9.3b)
circuit board: 10.0802cm x 3.92977cm
breadboards: 1

parts:
  Rp5 = Resistor [tolerance=±5% resistance=1k package=THT]
  Rp6 = Resistor [tolerance=±5% resistance=1k package=THT]
  Rp7 = Resistor [tolerance=±5% resistance=1k package=THT]
  Rp8 = Resistor [tolerance=±5% resistance=1k package=THT]
  Composant1 = Arduino Nano (Rev3.0) [part_number=Arduino]
  J1 = rounded female pin header, 4 pins [form="♀ (female rounded)"]
  J2 = rounded female pin header, 4 pins [form="♀ (female rounded)"]
  R1 = Resistor [tolerance=±1% resistance=270 package=THT]
  R2 = Resistor [tolerance=±1% resistance=270 package=THT]
  R3 = Resistor [tolerance=±1% resistance=150 package=THT]
  R4 = Resistor [tolerance=±1% resistance=150 package=THT]
  Raspberry_Pi1 = Raspberry Pi 2
  C1 = Ceramic Capacitor [capacitance=33nF voltage=16V package="200 mil [THT, multilayer]"]
  C2 = Ceramic Capacitor [capacitance=33nF voltage=16V package="200 mil [THT, multilayer]"]
  C3 = Electrolytic Capacitor [capacitance=10µF voltage=20V package="100 mil [THT, electrolytic]"]
  C4 = Electrolytic Capacitor [capacitance=10µF voltage=20V package="100 mil [THT, electrolytic]"]
  J5 = rounded female pin header, 6 pins [form="♀ (female rounded)"]
  J6 = rounded female pin header, 12 pins [form="♀ (female rounded)"]
  R5 = Resistor [tolerance=±5% resistance=150 package=THT]
  R6 = Resistor [tolerance=±5% resistance=150 package=THT]
  R7 = Resistor [tolerance=±5% resistance=150 package=THT]
  R8 = Resistor [tolerance=±5% resistance=150 package=THT]
  R9 = Resistor [tolerance=±5% resistance=150 package=THT]
  R10 = Resistor [tolerance=±5% resistance=150 package=THT]
  R11 = Resistor [tolerance=±5% resistance=150 package=THT]
  R12 = Resistor [tolerance=±5% resistance=150 package=THT]
  R13 = Resistor [tolerance=±5% resistance=150 package=THT]
  J7 = rounded female pin header, 13 pins [form="♀ (female rounded)"]
  SN74HC1 = SN74HC4851 [part_number=SN74HC4851 package="DIP (Dual Inline) [THT]"]
  D5 = Rectifier Diode [part_number=1N4001 package="100 mil [THT]"]
  D6 = Rectifier Diode [part_number=1N4001 package="100 mil [THT]"]
  D7 = Rectifier Diode [part_number=1N4001 package="100 mil [THT]"]
  D8 = Rectifier Diode [part_number=1N4001 package="100 mil [THT]"]
  Q2 = MOSFET-NCHANNEL [part_number=2N7000 package=to-92]
  Q3 = MOSFET-NCHANNEL [part_number=2N7000 package=to-92]
  Q4 = MOSFET-NCHANNEL [part_number=2N7000 package=to-92]
  Q5 = MOSFET-NCHANNEL [part_number=2N7000 package=to-92]
  J8 = female pin header, 4 pins [form="♀ (female)"]
  J9 = female pin header, 2 pins [form="♀ (female)"]
  J11 = female pin header, 2 pins [form="♀ (female)"]
  J12 = female pin header, 2 pins [form="♀ (female)"]
  J10 = female pin header, 2 pins [form="♀ (female)"]
  J3 = rounded female pin header, 5 pins [form="♀ (female rounded)"]

nets:
  5V: Rp5.Pin_0, Rp6.Pin_0, Composant1.5V, J2.pin1, Raspberry_Pi1.5V, SN74HC1.COM, SN74HC1.VCC, Q3.G, Q5.G, J10.pin1, J3.pin5
  N1: Rp5.Pin_1, Composant1.A4, J2.pin2, Q5.S
  N2: Rp6.Pin_1, Composant1.A5, J2.pin3, Q3.S
  N3: Rp7.Pin_0, J1.pin3, Raspberry_Pi1.GPIO2, Q4.S
  3V3: Rp7.Pin_1, Rp8.Pin_1, Composant1.3V3, J1.pin1, Raspberry_Pi1.3v3, Raspberry_Pi1.3V3, J5.pin5, D7.cathode, D8.cathode, Q2.G, Q4.G, J10.pin2
  N4: Rp8.Pin_0, J1.pin2, Raspberry_Pi1.GPIO3, Q2.S
  GND: Composant1.GND, J1.pin4, J2.pin4, R3.Pin_1, R4.Pin_0, Raspberry_Pi1.GND, C1.0, C2.0, J5.pin6, SN74HC1.GND, D5.anode, D6.anode, J11.pin2, J3.pin2, J3.pin4
  N5: Composant1.D2, R5.Pin_0
  N6: Composant1.D3, R6.Pin_0
  N7: Composant1.D4, R7.Pin_0
  N8: Composant1.D5, R9.Pin_0
  N9: Composant1.D6, R8.Pin_0
  N10: Composant1.D7, R10.Pin_0
  N11: Composant1.D8, R11.Pin_0
  N12: Composant1.D9, R13.Pin_0
  N13: Composant1.D10, R12.Pin_0
  N14: Composant1.D11/MOSI, J9.pin1
  N15: Composant1.D12/MISO, J9.pin2
  N16: Composant1.A3, SN74HC1.C
  N17: Composant1.A2, SN74HC1.B
  N18: Composant1.A1, SN74HC1.A
  N19: Composant1.A0, SN74HC1.INH
  N20: R1.Pin_0, R3.Pin_0, C1.1, C3.+
  N21: R1.Pin_1, Raspberry_Pi1.GPIO19
  N22: R2.Pin_0, R4.Pin_1, C2.1, C4.+
  N23: R2.Pin_1, Raspberry_Pi1.GPIO18
  N24: Raspberry_Pi1.GPIO4, J11.pin1
  N25: Raspberry_Pi1.GPIO17, J5.pin2
  N26: Raspberry_Pi1.GPIO27, J5.pin3
  N27: Raspberry_Pi1.GPIO22, J5.pin4
  N28: Raspberry_Pi1.GPIO10, J5.pin1
  N29: Raspberry_Pi1.GPIO5, J8.pin4
  N30: Raspberry_Pi1.GPIO6, J8.pin3
  N31: Raspberry_Pi1.GPIO13, J8.pin2
  N32: Raspberry_Pi1.GPIO26, J8.pin1
  N33: Raspberry_Pi1.GPIO16, J12.pin1
  N34: Raspberry_Pi1.GPIO12, J12.pin2
  N35: C3.-, D6.cathode, D8.anode, J3.pin1
  N36: C4.-, D5.cathode, D7.anode, J3.pin3
  N37: J6.pin1, SN74HC1.Y2
  N38: J6.pin2, R7.Pin_1, J7.pin6
  N39: J6.pin3, R6.Pin_1, J7.pin5
  N40: J6.pin4, SN74HC1.Y1
  N41: J6.pin5, SN74HC1.Y0
  N42: J6.pin6, R8.Pin_1, J7.pin7
  N43: J6.pin7, R12.Pin_1, J7.pin11
  N44: J6.pin8, R10.Pin_1, J7.pin9
  N45: J6.pin9, R11.Pin_1, J7.pin10
  N46: J6.pin10, R13.Pin_1, J7.pin12
  N47: J6.pin11, R5.Pin_1, J7.pin4
  N48: J6.pin12, SN74HC1.Y3
  N49: R9.Pin_1, J7.pin8
  N50: J7.pin1, SN74HC1.Y5
  N51: J7.pin2, SN74HC1.Y7
  N52: J7.pin3, SN74HC1.Y6
  N53: J7.pin13, SN74HC1.Y4
  N54: Q2.D, Q3.D
  N55: Q4.D, Q5.D

notes:
  I2C 3V3
  3V3 SDA SDC GND
  I2C 5V
  5V SDA SDC GND
  G5 G6 G13 G26
  Gnd
  D12 D11
  3V3 5V
  Gnd G4
  G12 G16
  I2C
  3V3
  5V
  Pi Up
  5V G L G R
  J6-5 / 0 > Digit 6
  J6-4 / 1 > Digit 7
  J6-1 / 2 > Digit 8
  J6-12 / 3 > Digit 5
  J7-13 / 4 > Digit 4
  J7-3 / 6 > Digit 3
  J7-2 / 7 > Digit 2
  J7-1 / 5 > Digit 1

custom parts:
  SN74HC4851: CMOS Multifunction Expandable 8-Input Gate
  Rectifier Diode: A standard rectifier diode
