# Fritzing sketch piClock4 (saved by Fritzing 0.9.3b)
circuit board: 10.0802cm x 3.92977cm
breadboards: 1

parts:
  Rp1 = Resistor [tolerance=±5% resistance=1k package=THT]
  Rp2 = Resistor [tolerance=±5% resistance=1k package=THT]
  Rp4 = Resistor [tolerance=±5% resistance=1k package=THT]
  Rp3 = Resistor [tolerance=±5% resistance=1k package=THT]
  J1 = rounded female pin header, 4 pins [form="♀ (female rounded)"]
  J2 = rounded female pin header, 4 pins [form="♀ (female rounded)"]
  R1 = Resistor [tolerance=±1% resistance=270 package=THT]
  R2 = Resistor [tolerance=±1% resistance=270 package=THT]
  R3 = Resistor [tolerance=±1% resistance=150 package=THT]
  R4 = Resistor [tolerance=±1% resistance=150 package=THT]
  Pi = Raspberry Pi 2
  C1 = Ceramic Capacitor [capacitance=33nF voltage=16V package="200 mil [THT, multilayer]"]
  C2 = Ceramic Capacitor [capacitance=33nF voltage=16V package="200 mil [THT, multilayer]"]
  C3 = Electrolytic Capacitor [capacitance=10µF voltage=20V package="100 mil [THT, electrolytic]"]
  C4 = Electrolytic Capacitor [capacitance=10µF voltage=20V package="100 mil [THT, electrolytic]"]
  J5 = rounded female pin header, 6 pins [form="♀ (female rounded)"]
  J6 = rounded female pin header, 12 pins [form="♀ (female rounded)"]
  J7 = rounded female pin header, 13 pins [form="♀ (female rounded)"]
  D1 = Rectifier Diode [part_number=1N4001 package="100 mil [THT]"]
  D2 = Rectifier Diode [part_number=1N4001 package="100 mil [THT]"]
  D3 = Rectifier Diode [part_number=1N4001 package="100 mil [THT]"]
  D4 = Rectifier Diode [part_number=1N4001 package="100 mil [THT]"]
  J3 = rounded female pin header, 5 pins [form="♀ (female rounded)"]
  Arduino_Nano = Arduino Nano (Rev3.0) [part_number=Arduino]
  U1 = MAX7219 [package=dil24]
  R5 = Resistor [tolerance=±5% resistance=22k package=THT]
  C5 = Ceramic Capacitor [capacitance=100nF package="100 mil [THT, multilayer]"]
  Q4 = 2N7000 NCH MOSFET [part_number=2N7000 package=to-92]
  Q3 = 2N7000 NCH MOSFET [part_number=2N7000 package=to-92]
  Q2 = 2N7000 NCH MOSFET [part_number=2N7000 package=to-92]
  Q1 = 2N7000 NCH MOSFET [part_number=2N7000 package=to-92]
  J16 = rounded female pin header, 2 pins [form="♀ (female rounded)"]
  DHT = rounded female pin header, 3 pins [form="♀ (female rounded)"]
  J13 = rounded female pin header, 2 pins [form="♀ (female rounded)"]
  J17 = rounded female pin header, 6 pins [form="♀ (female rounded)"]
  J12 = rounded female pin header, 2 pins [form="♀ (female rounded)"]
  J15 = rounded female pin header, 2 pins [form="♀ (female rounded)"]
  J8 = rounded female pin header, 4 pins [form="♀ (female rounded)"]
  J11 = rounded female pin header, 2 pins [form="♀ (female rounded)"]

nets:
  5V: Rp1.Pin_0, Rp2.Pin_0, J2.pin1, Pi.5V, J3.pin5, Arduino_Nano.5V, U1.VCC, R5.Pin_0, C5.1, Q3.G, Q2.G, DHT.pin1, J17.pin6
  N1: Rp1.Pin_1, J2.pin2, Arduino_Nano.A4, Q3.S
  N2: Rp2.Pin_1, J2.pin3, Arduino_Nano.A5, Q2.S
  N3: Rp4.Pin_0, J1.pin3, Pi.GPIO2, Q4.S
  3V3: Rp4.Pin_1, Rp3.Pin_1, J1.pin1, Pi.3v3, Pi.3V3, J5.pin5, D3.cathode, D4.cathode, Arduino_Nano.3V3, Q4.G, Q1.G
  N4: Rp3.Pin_0, J1.pin2, Pi.GPIO3, Q1.S
  GND: J1.pin4, J2.pin4, R3.Pin_1, R4.Pin_0, Pi.GND, C1.0, C2.0, J5.pin6, D1.anode, D2.anode, J3.pin2, J3.pin4, Arduino_Nano.GND, U1.GND, U1.GND2, C5.0, DHT.pin3, J17.pin1, J11.pin2
  N5: R1.Pin_0, R3.Pin_0, C1.1, C3.+
  N6: R1.Pin_1, Pi.GPIO19
  N7: R2.Pin_0, R4.Pin_1, C2.1, C4.+
  N8: R2.Pin_1, Pi.GPIO18
  N9: Pi.GPIO4, J11.pin1
  N10: Pi.GPIO17, J5.pin2
  N11: Pi.GPIO27, J5.pin3
  N12: Pi.GPIO22, J5.pin4
  N13: Pi.GPIO10, J5.pin1
  N14: Pi.GPIO5, J8.pin4
  N15: Pi.GPIO6, J8.pin3
  N16: Pi.GPIO13, J8.pin2
  N17: Pi.GPIO26, J8.pin1
  N18: Pi.GPIO16, J12.pin1
  N19: Pi.GPIO12, J12.pin2
  N20: Pi.GPIO15, J15.pin1
  N21: Pi.GPIO14, J15.pin2
  N22: C3.-, D2.cathode, D4.anode, J3.pin1
  N23: C4.-, D1.cathode, D3.anode, J3.pin3
  N24: J6.pin1, U1.SEGDP
  N25: J6.pin2, J7.pin6, U1.DIG3
  N26: J6.pin3, J7.pin5, U1.DIG2
  N27: J6.pin4, U1.SEGG
  N28: J6.pin5, U1.SEGF
  N29: J6.pin6, J7.pin7, U1.DIG4
  N30: J6.pin7, J7.pin11, U1.DIG1
  N31: J6.pin8, J7.pin9, U1.DIG0
  N32: J6.pin9, J7.pin10, U1.DIG7
  N33: J6.pin10, J7.pin12, U1.DIG5
  N34: J6.pin11, J7.pin4, U1.DIG6
  N35: J6.pin12, U1.SEGE
  N36: J7.pin1, U1.SEGA
  N37: J7.pin2, U1.SEGB
  N38: J7.pin3, U1.SEGC
  N39: J7.pin8, Arduino_Nano.D5
  N40: J7.pin13, U1.SEGD
  N41: Arduino_Nano.D1/TX, J13.pin1
  N42: Arduino_Nano.D0/RX, J13.pin2
  N43: Arduino_Nano.D2, DHT.pin2
  N44: Arduino_Nano.D3, J16.pin1
  N45: Arduino_Nano.D4, J16.pin2
  N46: Arduino_Nano.D6, J17.pin2
  N47: Arduino_Nano.D7, J17.pin3
  N48: Arduino_Nano.D8, J17.pin4
  N49: Arduino_Nano.D9, J17.pin5
  N50: Arduino_Nano.D10, U1.DIN
  N51: Arduino_Nano.D11/MOSI, U1.CLK
  N52: Arduino_Nano.D12/MISO, U1.LOAD
  N53: U1.ISET, R5.Pin_1
  N54: Q4.D, Q3.D
  N55: Q2.D, Q1.D

notes:
  I2C 3V3
  3V3 SDA SDC GND
  I2C 5V
  5V SDA SDC GND
  G5 G6 G13 G26
  Gnd
  Gnd G4
  G12 G16
  I2C
  3V3
  5V
  Pi Up
  5V G L G R
  J6-5 / 0 > Digit 6
  J6-4 / 1 > Digit 7
  J6-1 / 2 > Digit 8
  J6-12 / 3 > Digit 5
  J7-13 / 4 > Digit 4
  J7-3 / 6 > Digit 3
  J7-2 / 7 > Digit 2
  J7-1 / 5 > Digit 1
  RX TX Arduino
  TX RX Pi
  5V D GND
  D4 D3
  5V D9 D8 D7 D6 GND

custom parts:
  Rectifier Diode: A standard rectifier diode
  MAX7219: 8-digit, 8-segment LED display driver, serial input
  2N7000 NCH MOSFET: 2N7000 NMOS footprint
